# Fritzing sketch Moratorius-Holmes-O-Matic (saved by Fritzing 1.0.4)
perfboards: 3

parts:
  S2 = Taiway 100-SP-X-T1 SPDT Miniature Toggle Switch [part_number=100-SP-X-T1-0-0-B1-M2 package=THT]
  TP1 = TP4056 [chip_label=TP4056 package="DIP (Dual Inline) [THT]"]
  M1 = MT3608 Module
  BAT1 = 18650 battery holder [package=battery-18650-kit]
  LED2 = smd LED [color="Orange (620nm)" package="0603 [SMD]"]  # not connected
  LED1 = prefix0000
  LED1_2 = prefix0000
  LED1_3 = prefix0000
  LED1_4 = prefix0000
  LED1_5 = prefix0000
  LED1_6 = prefix0000
  LED1_7 = prefix0000
  LED1_8 = prefix0000
  LED1_9 = prefix0000
  LED1_10 = prefix0000
  U7 = JST XH 3A Male [chip_label=? package=THT]
  Bauteil4 = I2C level shifter bidirectional
  IC4 = IC, DIP package, 8 pins [chip_label=4151]
  U8 = JST-XH-6A
  J14 = JST XH 2A male [form="♂ (male)" package=THT]
  Bauteil6 = I2C level shifter bidirectional
  IC6 = MCP23017 I2C I/O Expander
  Q3 = ULN2803 Darlington Array
  R13 = Resistor [tolerance=±5% power=0.25W resistance=470 package=THT]
  R14 = Resistor [tolerance=±5% power=0.25W resistance=470 package=THT]
  R15 = Resistor [tolerance=±5% power=0.25W resistance=470 package=THT]
  R16 = Resistor [tolerance=±5% power=0.25W resistance=470 package=THT]
  J19 = JST XH 2A male [form="♂ (male)" package=THT]
  J20 = JST XH 2A male [form="♂ (male)" package=THT]
  J21 = JST XH 2A male [form="♂ (male)" package=THT]
  J22 = JST XH 2A male [form="♂ (male)" package=THT]
  U11 = JST-XH-6A
  J23 = JST XH 2A male [form="♂ (male)" package=THT]
  J24 = JST XH 2A male [form="♂ (male)" package=THT]
  S4 = Round Pushbutton  # not connected
  S5 = Taiway 100-SP-X-T1 SPDT Miniature Toggle Switch [part_number=100-SP-X-T1-0-0-B1-M2 package=THT]  # not connected
  LED9 = smd LED [color="Orange (620nm)" package="0603 [SMD]"]  # not connected
  LED10 = smd LED [color="Orange (620nm)" package="0603 [SMD]"]  # not connected
  LED11 = smd LED [color="Orange (620nm)" package="0603 [SMD]"]  # not connected
  U13 = ESP32-38PinWide [part_number=ESP32-38PinWide]
  SERVO3 = Tower Pro SG90 servo [part_number=101246]  # not connected
  U14 = JST-XH-6A
  U15 = JST-XH-6A
  J25 = female pin header, 3 pins [form="♀ (female)"]
  U16 = JST XH 3A Male [chip_label=? package=THT]
  X1 = USB Connectors [package=s4b-ph]  # not connected

nets:
  N1: S2.COM, TP1.pin3
  N2: S2.L2, M1.pin2
  N3: TP1.pin4, BAT1.-
  N4: TP1.pin5, BAT1.+
  N5: TP1.pin6, M1.pin1
  N6: LED1.connector1, LED1_2.connector1, LED1_3.connector1, LED1_4.connector1, LED1_5.connector1, LED1_6.connector1, LED1_7.connector1, LED1_8.connector1, LED1_9.connector1, LED1_10.connector1, U7.pin3
  N7: LED1.connector2, LED1_2.connector4
  N8: LED1.connector3, LED1_2.connector3, LED1_3.connector3, LED1_4.connector3, LED1_5.connector3, LED1_6.connector3, LED1_7.connector3, LED1_8.connector3, LED1_9.connector3, LED1_10.connector3, U7.pin1
  N9: LED1_2.connector2, LED1_3.connector4
  N10: LED1_3.connector2, LED1_4.connector4
  N11: LED1_4.connector2, LED1_5.connector4
  N12: LED1_5.connector2, LED1_6.connector4
  N13: LED1_6.connector2, LED1_7.connector4
  N14: LED1_7.connector2, LED1_8.connector4
  N15: LED1_8.connector2, LED1_10.connector4
  N16: LED1_9.connector2, U7.pin2
  N17: LED1_9.connector4, LED1_10.connector2
  N18: Bauteil4.LV3, U8.pin5
  N19: Bauteil4.GND, IC4.pin4, IC4.pin7, U8.pin4, J14.pin1
  N20: Bauteil4.LV, U8.pin3
  N21: Bauteil4.LV2, U8.pin2
  N22: Bauteil4.LV1, U8.pin1
  N23: Bauteil4.HV1, IC4.pin1
  N24: Bauteil4.HV2, IC4.pin2
  N25: Bauteil4.HV, IC4.pin5, IC4.pin8, U8.pin6
  N26: IC4.pin6, J14.pin2
  N27: Bauteil6.LV3, U11.pin2
  GND: Bauteil6.GND, IC6.VSS, IC6.A0, IC6.A1, IC6.A2, Q3.GND, U11.pin3, J23.pin2, J24.pin2
  N28: Bauteil6.LV, U11.pin4
  N29: Bauteil6.LV2, U11.pin5
  N30: Bauteil6.LV1, U11.pin6
  N31: Bauteil6.HV1, IC6.SDA
  N32: Bauteil6.HV2, IC6.SCL
  N33: Bauteil6.HV, IC6.VDD, IC6.RESET, Q3.COMMON, J19.pin2, J20.pin2, J21.pin2, J22.pin2, U11.pin1
  N34: Bauteil6.HV3, IC6.INTB
  N35: IC6.GPB0, J23.pin1
  N36: IC6.GPB1, J24.pin1
  N37: IC6.GPA0, Q3.I8
  N38: IC6.GPA1, Q3.I7
  N39: IC6.GPA2, Q3.I6
  N40: IC6.GPA3, Q3.I5
  N41: IC6.GPA4, Q3.I4
  N42: IC6.GPA5, Q3.I3
  N43: IC6.GPA6, Q3.I2
  N44: IC6.GPA7, Q3.I1
  N45: Q3.O4, R14.Pin_1
  N46: Q3.O3, R13.Pin_1
  N47: Q3.O2, R15.Pin_1
  N48: Q3.O1, R16.Pin_1
  N49: R13.Pin_0, J20.pin1
  N50: R14.Pin_0, J21.pin1
  N51: R15.Pin_0, J22.pin1
  N52: R16.Pin_0, J19.pin1
  N53: U13.3.3, U14.pin3, U15.pin4
  N54: U13.GPIO34, U15.pin2
  N55: U13.GPIO32, J25.pin3
  N56: U13.GPIO33, U15.pin6
  N57: U13.GPIO27, U15.pin5
  N58: U13.GND, U14.pin4, U15.pin3, J25.pin1
  N59: U13.GPIO11, U16.pin3
  N60: U13.VIN, U14.pin6, U15.pin1, J25.pin2, U16.pin1
  N61: U13.GPIO16, U16.pin2
  N62: U13.GPIO5, U14.pin1
  N63: U13.GPIO18, U14.pin2
  N64: U13.GPIO23, U14.pin5

notes:
  POWER
  CRIME 8
  CRIME 7
  CRIME 6
  CRIME 5
  CRIME 4
  CRIME 3
  CRIME 2
  CRIME 1
  STRIP_1
  ARROW 2
  ARROW 1
  CS SCK 3V3 GND SDI 5V
  GND 0V-5V
  MILES
  ROTARY LED
  LANTERN 2
  LANTERN 1
  5V  INTB  GND  3V3  SCL  SDA
  BUTTON
  SWITCH
  IN/OUT BOARD
  METER BOARD
  SG90 MOTOR
  GND 5V PWM
  5V DIN GND
  NEOPIXEL
  BLUE VIOLET GREY
  MAIN BOARD

custom parts:
  TP4056: A DIP stand-in part for whatever IC you want. With 6 pins on a 300mil dual inline package (DIP) footprint.
  MT3608 Module: MT3608 Boost Converter Module Links: Aerosemi MT3608 2A Step Up Converter datasheet
  18650 battery holder: 18650 Battery Holder identical to the dual battery version.
  JST XH 3A Male: 2.54 Mm JST "XH" connector
  JST-XH-6A: JST XH 6A (2.54)
  JST XH 2A male: JST XH-2A
  MCP23017 I2C I/O Expander: The MCP23017 uses two i2c pins (these can be shared with other i2c devices), and in exchange gives you 16 general purpose pins. You can set each of 16 pins to be input, output, input with a pullup or open drain. There's even the ability to get an interrupt via an external pin when any of the inputs change so you don't have to keep polling the chip.
  ULN2803 Darlington Array: ULN2803 Darlington Transistor Array with Flyback Protection
  ESP32-38PinWide: Generic 38-Pin ESP32 with wide format (only access to one side of pins on a breadboard) based on Stephen Lilley's HiLetgo ESP-WROOM-32 ESP32 ESP-32S Development Board.
  Tower Pro SG90 servo: Original file by John De Cristofaro http://www.adafruit.com/products/1449 Adafruit Feedback Servo (Small) Edited by: e-radionica.com 28/9/2015
